// Logisim project ALU.circ as structural Verilog: 2 circuits, main circuit ALU
module ALU (
  input  [31:0] A,
  input  [31:0] B,
  input  [4:0] Shift,
  input  [3:0] Codop,
  input  CarryIn,
  output [31:0] S,
  output [3:0] Flags
);

  wire adder_3_cout, bitselector_3_out, bitselector_5_out, bitselector_6_out, bitselector_7_out, Bout,
       comparator_1_eq, comparator_2_eq, comparator_4_eq, comparator_5_eq, Cout, CoutWithoutCin, MoinsShift,
       not_2_out, not_5_out, not_6_out, not_7_out, not_8_out, not_9_out, NotBoutWithoutCin, opShift, SigneA,
       SigneB, subtractor_3_bout, vADD, vSUB;
  wire [3:0] adder_4_out;
  wire [4:0] subtractor_4_out, subtractor_5_out;
  wire [30:0] multiplexer_1_out;
  wire [31:0] AandB, AfoisB, AorB, AplusB, AplusBplusCin, AXorB, BandNotA, BmoinsA, BmoinsAplusCinMoins1,
       BShiftArithmetic, BShiftLeft, BShiftRight, BShiftRotRight, not_1_out, notA, ZeromoinsA;

  assign not_1_out = ~A;  // NOT_Gate not_1, 32 bits wide
  assign AandB = A & B;  // AND_Gate and_1, 32 bits wide
  assign AXorB = A ^ B;  // XOR_Gate xor_1, 32 bits wide
  Shifter #(.width(32)) shifter_1 (.in(B), .\dist (Shift), .out(BShiftLeft));
  Shifter #(.shift("lr"), .width(32)) shifter_2 (.in(B), .\dist (Shift), .out(BShiftRight));
  Shifter #(.shift("ar"), .width(32)) shifter_3 (.in(B), .\dist (Shift), .out(BShiftArithmetic));
  Adder #(.width(32)) adder_1 (.a(A), .b(B), .out(AplusBplusCin), .cin(CarryIn), .cout(Cout));
  not not_2 (not_2_out, CarryIn);
  Subtractor #(.width(32)) subtractor_1 (.a(B), .b(A), .out(BmoinsAplusCinMoins1), .bin(not_2_out), .bout(Bout));
  Shifter #(.shift("rr"), .width(32)) shifter_4 (.in(B), .\dist (Shift), .out(BShiftRotRight));
  Subtractor #(.width(32)) subtractor_2 (.a({32{1'b0}}), .b(A), .out(ZeromoinsA));  // open: bin, bout
  Subtractor #(.width(32)) subtractor_3 (.a(B), .b(A), .out(BmoinsA), .bout(subtractor_3_bout));  // open: bin
  Adder #(.width(32)) adder_2 (.a(A), .b(B), .out(AplusB), .cout(CoutWithoutCin));  // open: cin
  assign AorB = A | B;  // OR_Gate or_1, 32 bits wide
  Multiplier #(.width(32)) multiplier_1 (.a(A), .b(B), .out(AfoisB));  // open: cin, cout
  assign BandNotA = not_1_out & B;  // AND_Gate and_2, 32 bits wide
  assign notA = ~A;  // NOT_Gate not_3, 32 bits wide
  not not_4 (NotBoutWithoutCin, subtractor_3_bout);
  Multiplexer #(.enable("true"), .select(4), .width(32)) multiplexer_1 (
    .in0(S), .in1(S), .in2(S), .in3(S), .in4(S), .in5(S), .in6(S), .in7(S), .in8(AandB), .in9(S),
    .in10(BmoinsA), .in11(AplusB), .in12(S), .in13(S), .in14(S), .in15(S),
    .out({Flags[3], multiplexer_1_out}), .sel(Codop));  // open: en
  BitSelector #(.width(32)) bitselector_1 (.in(A), .out(SigneA), .sel({5{1'b1}}));
  BitSelector #(.width(32)) bitselector_2 (.in(B), .out(SigneB), .sel({5{1'b1}}));
  Multiplexer #(.select(4), .width(32)) multiplexer_2 (
    .in0(AandB), .in1(AXorB), .in2(BShiftLeft), .in3(BShiftRight), .in4(BShiftArithmetic),
    .in5(AplusBplusCin), .in6(BmoinsAplusCinMoins1), .in7(BShiftRotRight), .in8(B), .in9(ZeromoinsA),
    .in10(B), .in11(B), .in12(AorB), .in13(AfoisB), .in14(BandNotA), .in15(notA), .out(S), .sel(Codop));
  Adder #(.width(32)) adder_3 (.a(notA), .b(32'h1), .cout(adder_3_cout));  // open: out, cin
  Subtractor #(.width(5)) subtractor_4 (.a({5{1'b0}}), .b(Shift), .out(subtractor_4_out));  // open: bin, bout
  Subtractor #(.width(5)) subtractor_5 (.a(Shift), .b(5'b00001), .out(subtractor_5_out));  // open: bin, bout
  not not_5 (not_5_out, Bout);
  BitSelector #(.width(32)) bitselector_3 (.in(B), .out(bitselector_3_out), .sel(subtractor_4_out));
  BitSelector #(.width(32)) bitselector_4 (.in(B), .out(MoinsShift), .sel(subtractor_5_out));
  Comparator #(.width(1)) comparator_1 (.a(SigneA), .b(SigneB), .eq(comparator_1_eq));  // open: gt, lt
  BitSelector #(.width(32)) bitselector_5 (.in(AplusBplusCin), .out(bitselector_5_out), .sel(5'b00001));
  Multiplexer #(.enable("true"), .select(4)) multiplexer_3 (
    .in0(1'b0), .in1(1'b0), .in2(opShift), .in3(opShift), .in4(opShift), .in5(Cout), .in6(not_5_out),
    .in7(MoinsShift), .in8(1'b0), .in9(adder_3_cout), .in10(NotBoutWithoutCin), .in11(CoutWithoutCin),
    .in12(1'b0), .in13(1'b0), .in14(1'b0), .in15(1'b0), .out(Flags[1]), .sel(Codop));  // open: en
  Multiplexer multiplexer_4 (.in0(bitselector_3_out), .in1(MoinsShift), .out(opShift), .sel(not_7_out));
  Adder #(.width(4)) adder_4 (.a(Codop), .b(4'b0001), .out(adder_4_out));  // open: cin, cout
  Multiplexer #(.enable("true"), .select(4)) multiplexer_5 (
    .in0(1'b0), .in1(1'b0), .in2(1'b0), .in3(1'b0), .in4(1'b0), .in5(vADD), .in6(vSUB), .in7(1'b0),
    .in8(1'b0), .in9(vADD), .in10(vSUB), .in11(vADD), .in12(1'b0), .in13(1'b0), .in14(1'b0), .in15(1'b0),
    .out(Flags[0]), .sel(Codop));  // open: en
  not not_6 (not_6_out, comparator_2_eq);
  Comparator #(.width(1)) comparator_2 (.a(SigneB), .b(bitselector_5_out), .eq(comparator_2_eq));  // open: gt, lt
  Comparator #(.width(32)) comparator_3 (
    .a({32{1'b0}}), .b({Flags[3], multiplexer_1_out}), .eq(Flags[2]));  // open: gt, lt
  not not_7 (not_7_out, bitselector_6_out);
  BitSelector #(.width(4)) bitselector_6 (.in(adder_4_out), .out(bitselector_6_out), .sel(2'b01));
  not not_8 (not_8_out, comparator_1_eq);
  and and_3 (vADD, comparator_1_eq, not_6_out);
  BitSelector #(.width(32)) bitselector_7 (.in(BmoinsAplusCinMoins1), .out(bitselector_7_out), .sel(5'b00001));
  not not_9 (not_9_out, comparator_4_eq);
  Comparator #(.width(1)) comparator_4 (.a(SigneB), .b(bitselector_7_out), .eq(comparator_4_eq));  // open: gt, lt
  and and_4 (vSUB, not_8_out, not_9_out);
  Comparator #(.width(4)) comparator_5 (.a(Codop), .b(4'b0111), .eq(comparator_5_eq));  // open: gt, lt

  // Other names for the same wires on the sheet: Cin = CarryIn; V = Flags[0]; C = Flags[1]; Z = Flags[2];
  //   Sortie[31:0] = S

  // Notes on the sheet:
  //   PAS CORRECT
  //   Note: for ROR, C = N
  //   Note 2: assume that shift > 0 for LSL and LSR
endmodule

module BancRegistre (
  input  [31:0] DataIn,
  input  [2:0] RegA,
  input  [2:0] RegB,
  input  [2:0] RegDest,
  input  Clk,
  input  Reset,
  output [31:0] AOut,
  output [31:0] BOut,
  output [31:0] R0,
  output [31:0] R1,
  output [31:0] R2,
  output [31:0] R3,
  output [31:0] R4,
  output [31:0] R5,
  output [31:0] R6,
  output [31:0] R7
);

  wire decoder_1_out0, decoder_1_out1, decoder_1_out2, decoder_1_out3, decoder_1_out4, decoder_1_out5,
       decoder_1_out6, decoder_1_out7;

  Decoder #(.select(3)) decoder_1 (
    .out0(decoder_1_out0), .out1(decoder_1_out1), .out2(decoder_1_out2), .out3(decoder_1_out3),
    .out4(decoder_1_out4), .out5(decoder_1_out5), .out6(decoder_1_out6), .out7(decoder_1_out7), .sel(RegDest));  // open: en
  Multiplexer #(.select(3), .width(32)) multiplexer_1 (
    .in0(R0), .in1(R1), .in2(R2), .in3(R3), .in4(R4), .in5(R5), .in6(R6), .in7(R6), .out(AOut), .sel(RegA));
  Register #(.width(32)) register_1 (.D(DataIn), .en(decoder_1_out0), .clk(Clk), .Q(R0), .clr(Reset));
  Register #(.width(32)) register_2 (.D(DataIn), .en(decoder_1_out2), .clk(Clk), .Q(R2), .clr(Reset));
  Register #(.width(32)) register_3 (.D(DataIn), .en(decoder_1_out4), .clk(Clk), .Q(R4), .clr(Reset));
  Register #(.width(32)) register_4 (.D(DataIn), .en(decoder_1_out6), .clk(Clk), .Q(R6), .clr(Reset));
  Register #(.width(32)) register_5 (.D(DataIn), .en(decoder_1_out1), .clk(Clk), .Q(R1), .clr(Reset));
  Register #(.width(32)) register_6 (.D(DataIn), .en(decoder_1_out3), .clk(Clk), .Q(R3), .clr(Reset));
  Register #(.width(32)) register_7 (.D(DataIn), .en(decoder_1_out5), .clk(Clk), .Q(R5), .clr(Reset));
  Register #(.width(32)) register_8 (.D(DataIn), .en(decoder_1_out7), .clk(Clk), .Q(R7), .clr(Reset));
  Multiplexer #(.select(3), .width(32)) multiplexer_2 (
    .in0(R0), .in1(R1), .in2(R2), .in3(R3), .in4(R4), .in5(R5), .in6(R6), .in7(R6), .out(BOut), .sel(RegB));
endmodule
