// Logisim project Ctl_Data_Processing.circ as structural Verilog: 2 circuits, main circuit Data_Processing
module Data_Processing (
  input  Enable,
  input  [15:0] Instruction,
  output [2:0] Rd,
  output [2:0] Rn,
  output [2:0] Rm,
  output [3:0] ALU_Opcode,
  output [3:0] Flags_Update_Mask
);

  wire C, N, V, Z;
  wire [2:0] R3_5;
  wire [15:10] multiplexer_1_out;

  Multiplexer #(.width(16)) multiplexer_1 (
    .in0({16{1'b0}}), .in1(Instruction), .out({multiplexer_1_out, ALU_Opcode, R3_5, Rd}), .sel(Enable));
  FlagMaskDecodeur flagmaskdecodeur_1 (.Codop(ALU_Opcode), .N(N), .Z(Z), .C(C), .V(V));
  Multiplexer #(.select(4), .width(3)) multiplexer_2 (
    .in0(R3_5), .in1(R3_5), .in2(R3_5), .in3(R3_5), .in4(R3_5), .in5(R3_5), .in6(R3_5), .in7(R3_5),
    .in8(R3_5), .in9(R3_5), .in10(R3_5), .in11(R3_5), .in12(R3_5), .in13(Rd), .in14(R3_5), .in15(R3_5),
    .out(Rm), .sel(ALU_Opcode));
  Multiplexer #(.width(4)) multiplexer_3 (.in0(4'b0000), .in1({N, Z, C, V}), .out(Flags_Update_Mask), .sel(Enable));
  Multiplexer #(.select(4), .width(3)) multiplexer_4 (
    .in0(Rd), .in1(Rd), .in2(Rd), .in3(Rd), .in4(Rd), .in5(Rd), .in6(Rd), .in7(Rd), .in8(Rd), .in9(R3_5),
    .in10(Rd), .in11(Rd), .in12(Rd), .in13(R3_5), .in14(Rd), .in15(Rd), .out(Rn), .sel(ALU_Opcode));

  // Other names for the same wires on the sheet: R0_2[2:0] = Rd; Opcode[3:0] = ALU_Opcode

  // Notes on the sheet:
  //   Pull output low on Enable = 0
endmodule

module FlagMaskDecodeur (
  input  [3:0] Codop,
  output N,
  output Z,
  output C,
  output V
);

  wire and_1_out, and_2_out, and_3_out, and_4_out, not_1_out, not_2_out, not_3_out, not_4_out;

  not not_1 (not_1_out, Codop[3]);
  not not_2 (not_2_out, Codop[2]);
  not not_3 (not_3_out, Codop[1]);
  not not_4 (not_4_out, Codop[0]);
  or or_1 (C, not_1_out, not_2_out, not_4_out, Codop[1]);
  and and_1 (and_1_out, not_1_out, Codop[2], not_3_out, Codop[0]);
  and and_2 (and_2_out, not_1_out, Codop[2], Codop[1], not_4_out);
  and and_3 (and_3_out, Codop[3], not_2_out, Codop[0]);
  and and_4 (and_4_out, Codop[3], not_2_out, Codop[1]);
  or or_2 (V, and_1_out, and_2_out, and_3_out, and_4_out);

  assign N = 1'b1;
  assign Z = 1'b1;
endmodule
