// Logisim project Ctl_Conditional.circ as structural Verilog: 1 circuit, main circuit Conditional
module Conditional (
  input  Enable,
  input  [15:0] Instruction,
  input  Z,
  input  C,
  input  N,
  input  V,
  output [10:0] Offset,
  output Verified
);

  wire and_3_out, CC, comparator_2_eq, comparator_3_eq, comparator_4_eq, comparator_5_eq, comparator_6_eq,
       GE, GT, HI, LE, LS, LT, multiplexer_2_out, NE, not_5_out, not_6_out, not_8_out, not_9_out, PL, Result,
       VC;
  wire [10:0] bit_extender_1_out, multiplexer_4_out;

  not not_1 (NE, Z);
  not not_2 (CC, C);
  not not_3 (PL, N);
  not not_4 (VC, V);
  not not_5 (not_5_out, Z);
  not not_6 (not_6_out, C);
  and and_1 (HI, C, not_5_out);
  or or_1 (LS, not_6_out, Z);
  Comparator #(.width(1)) comparator_1 (.a(N), .b(V), .eq(GE));  // open: gt, lt
  not not_7 (LT, comparator_2_eq);
  Comparator #(.width(1)) comparator_2 (.a(N), .b(V), .eq(comparator_2_eq));  // open: gt, lt
  Multiplexer #(.select(4)) multiplexer_1 (
    .in0(Z), .in1(NE), .in2(C), .in3(CC), .in4(N), .in5(PL), .in6(V), .in7(VC), .in8(HI), .in9(LS),
    .in10(GE), .in11(LT), .in12(GT), .in13(LE), .in14(1'b1), .out(Result), .sel(Instruction[11:8]));  // open: in15
  not not_8 (not_8_out, Z);
  and and_2 (GT, not_8_out, comparator_3_eq);
  Comparator #(.width(1)) comparator_3 (.a(N), .b(V), .eq(comparator_3_eq));  // open: gt, lt
  or or_2 (LE, Z, not_9_out);
  not not_9 (not_9_out, comparator_4_eq);
  Comparator #(.width(1)) comparator_4 (.a(N), .b(V), .eq(comparator_4_eq));  // open: gt, lt
  Multiplexer multiplexer_2 (.in0(Result), .in1(1'b1), .out(multiplexer_2_out), .sel(comparator_5_eq));
  Comparator #(.width(4)) comparator_5 (.a(Instruction[15:12]), .b(4'b1110), .eq(comparator_5_eq));  // open: gt, lt
  assign bit_extender_1_out = {{3{Instruction[7]}}, Instruction[7:0]};  // Bit_Extender bit_extender_1
  Comparator #(.width(4)) comparator_6 (.a(Instruction[15:12]), .b(4'b1110), .eq(comparator_6_eq));  // open: gt, lt
  Multiplexer multiplexer_3 (.in0(1'b0), .in1(multiplexer_2_out), .out(Verified), .sel(Enable));
  Multiplexer #(.width(11)) multiplexer_4 (
    .in0(bit_extender_1_out), .in1(Instruction[10:0]), .out(multiplexer_4_out), .sel(comparator_6_eq));
  Multiplexer #(.width(11)) multiplexer_5 (.in0({11{1'b0}}), .in1(multiplexer_4_out), .out(Offset), .sel(and_3_out));
  and and_3 (and_3_out, Enable, Verified);

  // Other names for the same wires on the sheet: CS = C; EQ = Z; imm8[7:0] = Instruction[7:0];
  //   imm11[10:0] = Instruction[10:0]; Condition[3:0] = Instruction[11:8]; codop[3:0] = Instruction[15:12]; MI = N;
  //   VS = V
endmodule
