// Logisim project Ctl_Load_Store.circ as structural Verilog: 1 circuit, main circuit Load_Store
module Load_Store (
  input  Enable,
  input  [15:0] Instruction,
  input  Clk,
  input  Reset,
  input  [31:0] Stack_Pointer,
  output Store,
  output Load,
  output PC_Hold,
  output [2:0] Rmd,
  output [31:0] RAM_Addr
);

  wire and_1_out, not_1_out, not_2_out;
  wire [31:0] RAM_Addr_Raw;

  Adder #(.width(32)) adder_1 (
    .a(Stack_Pointer), .b({{24{1'b0}}, Instruction[7:0]}), .out(RAM_Addr_Raw));  // open: cin, cout
  not not_1 (not_1_out, PC_Hold);
  Register #(.width(1)) register_1 (.D(and_1_out), .en(Enable), .clk(Clk), .Q(PC_Hold), .clr(Reset));
  and and_1 (and_1_out, not_1_out, Load);
  not not_2 (not_2_out, Instruction[11]);
  Multiplexer multiplexer_1 (.in0(1'b0), .in1(Instruction[11]), .out(Load), .sel(Enable));
  Multiplexer multiplexer_2 (.in0(1'b0), .in1(not_2_out), .out(Store), .sel(Enable));
  Multiplexer #(.width(3)) multiplexer_3 (.in0(3'b000), .in1(Instruction[10:8]), .out(Rmd), .sel(Enable));
  Multiplexer #(.width(32)) multiplexer_4 (.in0({32{1'b0}}), .in1(RAM_Addr_Raw), .out(RAM_Addr), .sel(Enable));

  // Other names for the same wires on the sheet: imm8[7:0] = Instruction[7:0]; Rt_Raw[2:0] = Instruction[10:8];
  //   CodopBit = Instruction[11]; Rt[2:0] = Rmd

  // Notes on the sheet:
  //   Instruction: pull=down
  //   Delay load and hold PC for 1 cycle for the RAM to send out requested data 
endmodule
