// Logisim project Ctl_Opcode_Decoder.circ as structural Verilog: 1 circuit, main circuit Opcode_Decoder
module Opcode_Decoder (
  input  [5:0] Opcode,
  output Shift,
  output Data_Processing,
  output Load_Store,
  output SP_Address,
  output Conditional
);

  wire or_1_out;

  and and_1 (Shift, ~Opcode[5], ~Opcode[4]);  // AND_Gate
  and and_2 (Data_Processing, ~Opcode[5], Opcode[4], ~Opcode[3], ~Opcode[2], ~Opcode[1], ~Opcode[0]);  // AND_Gate
  and and_3 (Load_Store, Opcode[5], ~Opcode[4], ~Opcode[3], Opcode[2]);  // AND_Gate
  and and_4 (SP_Address, Opcode[5], ~Opcode[4], Opcode[3], Opcode[2]);  // AND_Gate
  and and_5 (Conditional, Opcode[5], Opcode[4], or_1_out);
  or or_1 (or_1_out, Opcode[3], Opcode[2]);

  // Notes on the sheet:
  //   Shift, add, sub, mov
  //   Load/Store
  //   SP Address
  //   Conditional branch
  //   Data Processing
endmodule
