// Logisim project Ctl_Shift_Add_Sub_Mov.circ as structural Verilog: 5 circuits, main circuit Shift_Add_Sub_Mov
module Shift_Add_Sub_Mov (
  input  Enable,
  input  [15:0] Instruction,
  output [3:0] Flags_Update_Mask,
  output Carry,
  output Imm32_Enable,
  output [2:0] Rm,
  output [2:0] Rn,
  output [2:0] Rd,
  output [4:0] Imm5,
  output [31:0] Imm32,
  output [3:0] ALU_Opcode
);

  wire and_1_out, and_2_out, and_3_out, and_4_out, imm32_8_5_1_imm32_enable, iscarry_1_carry_found,
       not_1_out, not_2_out, not_3_out, not_4_out, not_5_out, or_1_out, select_rm;
  wire [2:0] multiplexer_1_out, multiplexer_10_out, Rd_t, Rm_t, Rn_t;
  wire [3:0] alu_opcode_op_sub_1_alu_opcode, update_flag_1_flags;
  wire [4:0] imm32_8_5_1_imm5_sortie;
  wire [31:0] imm32_8_5_1_imm32;

  and and_1 (and_1_out, Instruction[13], Instruction[12]);
  Multiplexer #(.width(3)) multiplexer_1 (
    .in0(3'b000), .in1(Instruction[10:8]), .out(multiplexer_1_out), .sel(and_1_out));
  Multiplexer #(.width(3)) multiplexer_2 (.in0(multiplexer_1_out), .in1(Instruction[5:3]), .out(Rn_t), .sel(or_1_out));
  or or_1 (or_1_out, select_rm, and_2_out);
  and and_2 (and_2_out, Instruction[11], Instruction[12], not_1_out);
  not not_1 (not_1_out, Instruction[13]);
  imm32_8_5 imm32_8_5_1 (
    .Op(Instruction[13:11]), .Index_10(Instruction[10]), .imm_3(Instruction[8:6]), .imm_8(Instruction[7:0]),
    .imm5(Instruction[10:6]), .imm32_enable(imm32_8_5_1_imm32_enable), .imm32(imm32_8_5_1_imm32),
    .imm5_sortie(imm32_8_5_1_imm5_sortie));
  update_flag update_flag_1 (.op(Instruction[13:11]), .flags(update_flag_1_flags));
  isCarry iscarry_1 (.Op(Instruction[13:11]), .sub(Instruction[9]), .carry_found(iscarry_1_carry_found));
  alu_opcode_op_sub alu_opcode_op_sub_1 (
    .op(Instruction[13:11]), .sub(Instruction[9]), .ALU_Opcode(alu_opcode_op_sub_1_alu_opcode));
  not not_2 (not_2_out, Instruction[11]);
  not not_3 (not_3_out, Instruction[13]);
  not not_4 (not_4_out, Instruction[13]);
  not not_5 (not_5_out, Instruction[12]);
  Multiplexer #(.width(4)) multiplexer_3 (
    .in0(4'b0000), .in1(update_flag_1_flags), .out(Flags_Update_Mask), .sel(Enable));
  Multiplexer multiplexer_4 (.in0(1'b0), .in1(iscarry_1_carry_found), .out(Carry), .sel(Enable));
  Multiplexer multiplexer_5 (.in0(1'b0), .in1(imm32_8_5_1_imm32_enable), .out(Imm32_Enable), .sel(Enable));
  Multiplexer #(.width(3)) multiplexer_6 (.in0(3'b000), .in1(Rm_t), .out(Rm), .sel(Enable));
  Multiplexer #(.width(3)) multiplexer_7 (.in0(3'b000), .in1(Rn_t), .out(Rn), .sel(Enable));
  Multiplexer #(.width(3)) multiplexer_8 (.in0(3'b000), .in1(Rd_t), .out(Rd), .sel(Enable));
  Multiplexer #(.width(4)) multiplexer_9 (
    .in0(4'b0000), .in1(alu_opcode_op_sub_1_alu_opcode), .out(ALU_Opcode), .sel(Enable));
  Multiplexer #(.width(3)) multiplexer_10 (
    .in0(Instruction[8:6]), .in1(3'b000), .out(multiplexer_10_out), .sel(Instruction[10]));
  and and_3 (and_3_out, not_2_out, not_3_out);
  and and_4 (and_4_out, not_4_out, not_5_out);
  Multiplexer #(.width(5)) multiplexer_11 (.in0({5{1'b0}}), .in1(imm32_8_5_1_imm5_sortie), .out(Imm5), .sel(Enable));
  Multiplexer #(.width(32)) multiplexer_12 (.in0({32{1'b0}}), .in1(imm32_8_5_1_imm32), .out(Imm32), .sel(Enable));
  Multiplexer #(.width(3)) multiplexer_13 (
    .in0(multiplexer_10_out), .in1(Instruction[5:3]), .out(Rm_t), .sel(select_rm));
  or or_2 (select_rm, and_3_out, and_4_out);
  Multiplexer #(.width(3)) multiplexer_14 (
    .in0(Instruction[2:0]), .in1(Instruction[10:8]), .out(Rd_t), .sel(Instruction[13]));

  // Other names for the same wires on the sheet: Bits0_2[2:0] = Instruction[2:0]; Bits0_7[7:0] = Instruction[7:0];
  //   Bits3_5[2:0] = Instruction[5:3]; Bits6_8[2:0] = Instruction[8:6]; Bits6_10[4:0] = Instruction[10:6];
  //   Bits8_10[2:0] = Instruction[10:8]; Bits9_10[1:0] = Instruction[10:9]; index_9 = Instruction[9];
  //   index_10 = Instruction[10]; index_11 = Instruction[11]; op[2:0] = Instruction[13:11];
  //   index_12 = Instruction[12]; index_13 = Instruction[13]

  // Notes on the sheet:
  //   Note: ALU uses Rn register for shifts. Use Rn instead of Rm for shifts (immediate) here too
  //   Note 2: MOV uses RSB ALU opcode with Imm8 reversed so that it is copied to output register
  //   Note 3: Imm32_Enable forces the use of the immediate for Rm register
  //   Pull output low on Enable = 0
  //   only ADD and SUB use Rm
  //   Enable carry for SUB since it is reversed in ALU
  //   ALU will use Imm32 instead of Rm
endmodule

module update_flag (
  input  [2:0] op,
  output [3:0] flags
);

  wire and_1_out, and_2_out, and_3_out, not_1_out;

  not not_1 (not_1_out, op[2]);
  or or_1 (flags[1], not_1_out, op[0], op[1]);
  and and_1 (and_1_out, op[1], op[0]);
  and and_2 (and_2_out, op[2], op[0]);
  and and_3 (and_3_out, op[2], op[1]);
  or or_2 (flags[0], and_1_out, and_2_out, and_3_out);

  assign flags[3:2] = 2'b11;
endmodule

module alu_opcode_op_sub (
  input  [2:0] op,
  input  sub,
  output [3:0] ALU_Opcode
);

  wire and_2_out, and_3_out, and_4_out, and_5_out, and_6_out, and_7_out, not_1_out, not_2_out, not_3_out,
       not_4_out;

  not not_1 (not_1_out, op[2]);
  not not_2 (not_2_out, op[1]);
  not not_3 (not_3_out, op[0]);
  not not_4 (not_4_out, sub);
  and and_1 (ALU_Opcode[3], op[2], not_2_out);
  and and_2 (and_2_out, not_1_out, not_2_out);
  and and_3 (and_3_out, op[0], sub);
  and and_4 (and_4_out, op[2], op[0]);
  and and_5 (and_5_out, op[2], not_3_out);
  and and_6 (and_6_out, not_1_out, not_2_out, op[0]);
  and and_7 (and_7_out, not_1_out, op[0], not_4_out);
  or or_1 (ALU_Opcode[1], and_2_out, and_3_out, and_4_out);
  or or_2 (ALU_Opcode[0], and_5_out, and_6_out, and_7_out);

  assign ALU_Opcode[2] = op[1];
endmodule

module isCarry (
  input  [2:0] Op,
  input  sub,
  output carry_found
);

  wire and_1_out, and_2_out;

  and and_1 (and_1_out, Op[1], Op[0], sub);
  and and_2 (and_2_out, Op[2], Op[1], Op[0]);
  or or_1 (carry_found, and_1_out, and_2_out);
endmodule

module imm32_8_5 (
  input  [2:0] Op,
  input  Index_10,
  input  [2:0] imm_3,
  input  [7:0] imm_8,
  input  [4:0] imm5,
  output imm32_enable,
  output [31:0] imm32,
  output [4:0] imm5_sortie
);

  wire and_1_out, and_2_out, and_3_out, and_4_out, not_1_out, not_2_out, not_3_out, or_1_out;
  wire [31:0] bit_extender_1_out, bit_extender_2_out, multiplexer_2_out, multiplexer_3_out, negator_1_out;

  not not_1 (not_1_out, Op[0]);
  assign bit_extender_1_out = {{29{1'b0}}, imm_3};  // Bit_Extender bit_extender_1
  assign bit_extender_2_out = {{24{1'b0}}, imm_8};  // Bit_Extender bit_extender_2
  Multiplexer #(.width(5)) multiplexer_1 (.in0({5{1'b0}}), .in1(imm5), .out(imm5_sortie), .sel(or_1_out));
  not not_2 (not_2_out, Op[1]);
  not not_3 (not_3_out, Op[2]);
  and and_1 (and_1_out, not_2_out, not_1_out);
  Negator #(.width(32)) negator_1 (.in(bit_extender_2_out), .out(negator_1_out));
  and and_2 (and_2_out, Op[0], Op[1], Index_10);
  Multiplexer #(.width(32)) multiplexer_2 (
    .in0(bit_extender_2_out), .in1(negator_1_out), .out(multiplexer_2_out), .sel(and_1_out));
  and and_3 (and_3_out, not_3_out, not_1_out);
  Multiplexer #(.width(32)) multiplexer_3 (
    .in0(bit_extender_1_out), .in1(multiplexer_2_out), .out(multiplexer_3_out), .sel(Op[2]));
  and and_4 (and_4_out, not_2_out, not_3_out);
  or or_1 (or_1_out, and_3_out, and_4_out);
  or or_2 (imm32_enable, Op[2], and_2_out);
  Multiplexer #(.width(32)) multiplexer_4 (.in0({32{1'b0}}), .in1(multiplexer_3_out), .out(imm32), .sel(imm32_enable));
endmodule
